# Fritzing sketch 28BYJ-48-driver_and_motor (saved by Fritzing 0.9.6b)

parts:
  Driver1 = 28BYJ-48 Driver Module [part_number=ULN2003 package=THT]
  SM1 = 28BYJ-48 Stepper Motor [part_number=28BYJ-48]
  IC1 = DIP - 28 pins [chip_label=IC package="DIP (Dual Inline) [THT]"]

nets:
  N1: Driver1.IN1, IC1.P19
  N2: Driver1.IN2, IC1.P20
  N3: Driver1.IN3, IC1.P21
  N4: Driver1.IN4, IC1.P22
  GND: Driver1.GND, IC1.GND
  N5: Driver1.Vmotor, IC1.VIN
  N6: Driver1.blue-pin, SM1.blue-pin
  N7: Driver1.pink-pin, SM1.pink-pin
  N8: Driver1.yellow-pin, SM1.yellow-pin
  N9: Driver1.orange-pin, SM1.orange-pin
  N10: Driver1.red-pin, SM1.red-pin

custom parts:
  28BYJ-48 Driver Module: Generic male header
  28BYJ-48 Stepper Motor: Unipolar Stepper Motor 28BYJ-48 Top coil - pink & orange Bottom coil - blue & yellow Common rail - red Connector pins: blue - pink - yellow - orange - red
  DIP - 28 pins: A DIP stand-in part for whatever IC you want. With 28 pins on a 300mil dual inline package (DIP) footprint.
