# Fritzing sketch PIR (saved by Fritzing 0.9.6b)
breadboards: 1

parts:
  IC16 = DIP - 28 pins [chip_label=IC package="DIP (Dual Inline) [THT]"]
  PIR2 = PIR sensor

nets:
  VIN: IC16.VIN, PIR2.VDD
  GND: IC16.GND, PIR2.GND
  N1: IC16.P13, PIR2.SIG

notes:
  RED = VCC (5V)
  BLACK = GND
  ORANGE = (Signal)

custom parts:
  DIP - 28 pins: A DIP stand-in part for whatever IC you want. With 28 pins on a 300mil dual inline package (DIP) footprint.
