# Fritzing sketch ina260 (saved by Fritzing 0.9.6b)
breadboards: 1

parts:
  IC6 = DIP - 28 pins [chip_label=IC package="DIP (Dual Inline) [THT]"]
  Part1 = INA 260
  LED1 = LED - 5mm [color="Red (633nm)" package="5 mm [THT]"]
  R1 = Resistor [tolerance=±5% resistance=100 package="0402 [SMD]"]

nets:
  GND: IC6.GND, Part1.GND, LED1.cathode
  3V3: IC6.3V3, Part1.VCC, Part1.IN+
  N1: IC6.P10, Part1.SCL
  N2: IC6.P9, Part1.SDA
  N3: Part1.IN-, R1.Pin_0
  N4: LED1.anode, R1.Pin_1

custom parts:
  DIP - 28 pins: A DIP stand-in part for whatever IC you want. With 28 pins on a 300mil dual inline package (DIP) footprint.
  INA 260: Rev. B, add copy
