# Fritzing sketch pycom_pysense (saved by Fritzing 0.9.9b)
circuit board: 8.46667cm x 5.64444cm
breadboards: 1

parts:
  IC1 = DIP - 44 pins [chip_label="Pysense 2.0X" package="DIP (Dual Inline) [THT]"]
  IC3 = pycom-finished [chip_label=Fipy]

nets:
  N1: IC1.P0, IC3.connector1
  N2: IC1.P1, IC3.connector2
  N3: IC1.P21, IC3.connector22
  N4: IC1.P22, IC3.connector23
  N5: IC1.3V3, IC3.connector25
  N6: IC1.GND, IC3.connector26
  N7: IC1.5V, IC3.connector27

notes:
  3.3V
  rail
  Pysense is used only as a programmer in this example. E.g. don't connect sensor pins/wires to it, all sensors should be connected on the breadboard and to the Fipy/Lopy4/Gpy

custom parts:
  DIP - 44 pins: A DIP stand-in part for whatever IC you want. With 44 pins on a 300mil dual inline package (DIP) footprint.
