# Fritzing sketch tilt (saved by Fritzing 0.9.6b)
breadboards: 1

parts:
  IC4 = DIP - 28 pins [chip_label=IC package="DIP (Dual Inline) [THT]"]
  S1 = TILT-SWITCH-SW-200D [package=reed_switch_plastic]

nets:
  N1: IC4.GND, S1.2
  N2: IC4.P15, S1.1

custom parts:
  DIP - 28 pins: A DIP stand-in part for whatever IC you want. With 28 pins on a 300mil dual inline package (DIP) footprint.
