# Fritzing sketch bme680 (saved by Fritzing 0.9.6b)
breadboards: 1

parts:
  IC5 = DIP - 28 pins [chip_label=IC package="DIP (Dual Inline) [THT]"]
  Part1 = INA 260

nets:
  VIN: IC5.VIN, Part1.VCC
  GND: IC5.GND, Part1.GND
  N1: IC5.P8, Part1.SCL
  N2: IC5.P7, Part1.SDA

custom parts:
  DIP - 28 pins: A DIP stand-in part for whatever IC you want. With 28 pins on a 300mil dual inline package (DIP) footprint.
  INA 260: Rev. B, add copy
