# Fritzing sketch Line_Follower (saved by Fritzing 0.9.3b)
breadboards: 1

parts:
  Mod1 = Raspberry Pi Pico W
  Part1 = KY-033 Line Follower Sensor [package="Breakout board"]

nets:
  N1: Mod1.pin_32, Part1.S
  N2: Mod1.pin_36, Part1.V+
  N3: Mod1.pin_38, Part1.GND

notes:
  Your Sensor might differ from the one shown here. Ask a TA if you are unsure of how to connect.

custom parts:
  Raspberry Pi Pico W: Raspberry Pi Pico W. Based around the RP2040 microcontroller the Pico W is a low cost microcontroller device bringing Raspberry Pi quality, cost, and easy of use to the microcontroller space. The areas marked KEEPOUT in pcb silkscreen should not have traces running through them to avoid shorts on a soldered in module!
  KY-033 Line Follower Sensor: Tracing Black White Line Hunting Sensor Module For Arduino. This is KY-033 tracking sensor. The KY-033 measures the intensity of infrared radiation and delivers it as an analog output voltage. Operating voltage: 2.5 - 12V(cannot over12V), working current: 18mA-20mA at 5V. Enhanced accuracy. Documents: http://www.vishay.com/docs/83760/tcrt5000.pdf
