# Fritzing sketch Hall_Sensor_Digital_Analog (saved by Fritzing 0.9.3b)
breadboards: 1

parts:
  Mod1 = Raspberry Pi Pico W
  Part3 = KY-024 Linear Hall Magnetic Sensor Module [package="Breakout board"]

nets:
  N1: Mod1.pin_31, Part3.D0
  N2: Mod1.pin_32, Part3.A0
  N3: Mod1.pin_36, Part3.+
  N4: Mod1.pin_38, Mod1.pin_42, Part3.G

notes:
  Your Sensor might differ from the one shown here. Ask a TA if you are unsure of how to connect.

custom parts:
  Raspberry Pi Pico W: Raspberry Pi Pico W. Based around the RP2040 microcontroller the Pico W is a low cost microcontroller device bringing Raspberry Pi quality, cost, and easy of use to the microcontroller space. The areas marked KEEPOUT in pcb silkscreen should not have traces running through them to avoid shorts on a soldered in module!
  KY-024 Linear Hall Magnetic Sensor Module: KEYES KY-024 Arduino Linear Hall Magnetic Sensor Module reacts iin the presence of a magnetic field.
