# Fritzing sketch Tilt_Switch (saved by Fritzing 0.9.3b)
breadboards: 1

parts:
  Mod1 = Raspberry Pi Pico W
  Part4 = KY-020 Tilt Switch Module [package="Breakout board"]

nets:
  N1: Mod1.pin_32, Part4.S
  N2: Mod1.pin_36, Part4.Vin
  N3: Mod1.pin_38, Part4.-

notes:
  Your Sensor might differ from the one shown here. Ask a TA if you are unsure of how to connect.

custom parts:
  Raspberry Pi Pico W: Raspberry Pi Pico W. Based around the RP2040 microcontroller the Pico W is a low cost microcontroller device bringing Raspberry Pi quality, cost, and easy of use to the microcontroller space. The areas marked KEEPOUT in pcb silkscreen should not have traces running through them to avoid shorts on a soldered in module!
  KY-020 Tilt Switch Module: KY-020 Arduino tilt switch sensor module. Closes the circuit when it is tilted to the side as long as it is moved with enough force and degree of inclination to activate the ball switch inside.
