# Fritzing sketch Knock_Sensor (saved by Fritzing 0.9.3b)
breadboards: 1

parts:
  Mod1 = Raspberry Pi Pico W
  Mod2 = KY-031 Knock Sensor Module [package="Breakout board"]

nets:
  N1: Mod1.pin_32, Mod2.S
  N2: Mod1.pin_36, Mod2.Vin
  N3: Mod1.pin_38, Mod1.pin_42, Mod2.-

notes:
  Your Sensor might differ from the one shown here. Ask a TA if you are unsure of how to connect.

custom parts:
  Raspberry Pi Pico W: Raspberry Pi Pico W. Based around the RP2040 microcontroller the Pico W is a low cost microcontroller device bringing Raspberry Pi quality, cost, and easy of use to the microcontroller space. The areas marked KEEPOUT in pcb silkscreen should not have traces running through them to avoid shorts on a soldered in module!
  KY-031 Knock Sensor Module: KY-031 Knock Sensor module. A vibration sensor that sends a signal when a knock/tap is detected.
