# Fritzing sketch LDR_Photo_Resistor (saved by Fritzing 0.9.3b)
breadboards: 1

parts:
  Mod1 = Raspberry Pi Pico W
  Part1 = KY-018 Photoresistor Module [package="Breakout board"]

nets:
  N1: Mod1.pin_32, Part1.S
  N2: Mod1.pin_36, Part1.Vin
  N3: Mod1.pin_38, Part1.-

notes:
  Your Sensor might differ from the one shown here. Ask a TA if you are unsure of how to connect.

custom parts:
  Raspberry Pi Pico W: Raspberry Pi Pico W. Based around the RP2040 microcontroller the Pico W is a low cost microcontroller device bringing Raspberry Pi quality, cost, and easy of use to the microcontroller space. The areas marked KEEPOUT in pcb silkscreen should not have traces running through them to avoid shorts on a soldered in module!
  KY-018 Photoresistor Module: KY-018 Photoresistor module, used to measure light intensity. It can determine the presence or absence of light.
