# Fritzing sketch PIR_Motion_Sensor (saved by Fritzing 0.9.3b)
breadboards: 1

parts:
  Mod1 = Raspberry Pi Pico W
  HC-SR1 = HC-SR501 Body Sensor Module

nets:
  N1: Mod1.pin_32, HC-SR1.OUT
  N2: Mod1.pin_36, HC-SR1.VCC
  N3: Mod1.pin_38, Mod1.pin_42, HC-SR1.GND

notes:
  Your Sensor might differ from the one shown here. Ask a TA if you are unsure of how to connect.

custom parts:
  Raspberry Pi Pico W: Raspberry Pi Pico W. Based around the RP2040 microcontroller the Pico W is a low cost microcontroller device bringing Raspberry Pi quality, cost, and easy of use to the microcontroller space. The areas marked KEEPOUT in pcb silkscreen should not have traces running through them to avoid shorts on a soldered in module!
  HC-SR501 Body Sensor Module: Pyroelectric Infrared PIR Motion Sensor Detector Module
