# Fritzing sketch Ultrasonic_Sensor (saved by Fritzing 0.9.3b)
breadboards: 1

parts:
  Mod1 = Raspberry Pi Pico W
  HC-SR04_Sensor_1 = HC-SR04 Ultrasonic Distance Sensor

nets:
  N1: Mod1.pin_31, HC-SR04_Sensor_1.TRIG
  N2: Mod1.pin_32, HC-SR04_Sensor_1.ECHO
  N3: Mod1.pin_38, Mod1.pin_42, HC-SR04_Sensor_1.GND
  N4: Mod1.pin_39, HC-SR04_Sensor_1.VCC

notes:
  Your Sensor might differ from the one shown here. Ask a TA if you are unsure of how to connect.
  We connected VCC to VSYS to get 5.0v that ultrasonic operates on

custom parts:
  Raspberry Pi Pico W: Raspberry Pi Pico W. Based around the RP2040 microcontroller the Pico W is a low cost microcontroller device bringing Raspberry Pi quality, cost, and easy of use to the microcontroller space. The areas marked KEEPOUT in pcb silkscreen should not have traces running through them to avoid shorts on a soldered in module!
