# Fritzing sketch CCS811andSHT31 (saved by Fritzing 0.9.3b)
breadboards: 1

parts:
  Mod1 = Raspberry Pi Pico W
  Mod2 = CJMCU-811
  J1 = SHT3X [form="♂ (male)" package=THT]

nets:
  N1: Mod1.pin_31, Mod2.SDA, J1.SDA/RH
  N2: Mod1.pin_32, Mod2.SCL, J1.SCL/T
  VCC: Mod1.pin_36, Mod2.VCC, J1.VIN
  GND: Mod1.pin_38, Mod1.pin_42, Mod2.GND, Mod2.WAK, J1.GND

notes:
  Your Sensor might differ from the one shown here. Ask a TA if you are unsure of how to connect.
  I2C port shared between CCS811 & SHT31

custom parts:
  Raspberry Pi Pico W: Raspberry Pi Pico W. Based around the RP2040 microcontroller the Pico W is a low cost microcontroller device bringing Raspberry Pi quality, cost, and easy of use to the microcontroller space. The areas marked KEEPOUT in pcb silkscreen should not have traces running through them to avoid shorts on a soldered in module!
  CJMCU-811: The CCS811 is an ultra-low power digital gas sensor solution which integrates a metal oxide (MOX) gas sensor to detect a wide range of Volatile Organic Compounds (VOCs) for indoor air quality monitoring with a microcontroller unit (MCU), which includes an Analog-to-Digital converter (ADC), and an I²C interface.
  SHT3X: SHT31 SHT31-D Temperature & Humidity Sensor Breakout
