# Fritzing sketch BME680 (saved by Fritzing 0.9.3b)
breadboards: 1

parts:
  Mod1 = Raspberry Pi Pico W
  J1 = BME680 [form="♂ (male)" package=THT]

nets:
  N1: Mod1.pin_31, J1.SDA
  N2: Mod1.pin_32, J1.SCL
  N3: Mod1.pin_33, Mod1.pin_38, J1.GND
  N4: Mod1.pin_36, J1.VCC

notes:
  Your Sensor might differ from the one shown here. Ask a TA if you are unsure of how to connect.

custom parts:
  Raspberry Pi Pico W: Raspberry Pi Pico W. Based around the RP2040 microcontroller the Pico W is a low cost microcontroller device bringing Raspberry Pi quality, cost, and easy of use to the microcontroller space. The areas marked KEEPOUT in pcb silkscreen should not have traces running through them to avoid shorts on a soldered in module!
  BME680: BME680 - TEMPERATURE, HUMIDITY, PRESSURE AND GAS SENSOR.
