# Fritzing sketch button (saved by Fritzing 0.9.6b)
breadboards: 1

parts:
  IC4 = DIP - 28 pins [chip_label=IC package="DIP (Dual Inline) [THT]"]
  R1 = Resistor [tolerance=±5% resistance=10k package=THT]
  S1 = Pushbutton [package="[SMD]"]

nets:
  N1: IC4.GND, IC4.P13, R1.Pin_0
  N2: IC4.3V3, S1.Pin_3, S1.Pin_4
  N3: R1.Pin_1, S1.Pin_1, S1.Pin_2

custom parts:
  DIP - 28 pins: A DIP stand-in part for whatever IC you want. With 28 pins on a 300mil dual inline package (DIP) footprint.
