# Fritzing sketch buzzer (saved by Fritzing 0.9.6b)
breadboards: 1

parts:
  IC2 = DIP - 28 pins [chip_label=IC package="DIP (Dual Inline) [THT]"]
  Part1 = Passive Buzzer

nets:
  N1: IC2.VIN, Part1.NC
  GND: IC2.GND, Part1.GND

custom parts:
  DIP - 28 pins: A DIP stand-in part for whatever IC you want. With 28 pins on a 300mil dual inline package (DIP) footprint.
