# Fritzing sketch oled ssd1327 (saved by Fritzing 0.9.6b)
breadboards: 1

parts:
  IC6 = DIP - 28 pins [chip_label=IC package="DIP (Dual Inline) [THT]"]
  OLED_I2C1 = OLED 128x64 I2C Monochrome Display

nets:
  GND: IC6.GND, OLED_I2C1.GND
  3V3: IC6.3V3, OLED_I2C1.VDD
  N1: IC6.P10, OLED_I2C1.SCK
  N2: IC6.P9, OLED_I2C1.SDA

custom parts:
  DIP - 28 pins: A DIP stand-in part for whatever IC you want. With 28 pins on a 300mil dual inline package (DIP) footprint.
