# Fritzing sketch HC-SR04 (saved by Fritzing 0.9.6b)
breadboards: 1

parts:
  IC1 = DIP - 28 pins [chip_label=IC package="DIP (Dual Inline) [THT]"]
  hc-sr1 = hc-sr04

nets:
  VIN: IC1.VIN, hc-sr1.VCC
  GND: IC1.GND, hc-sr1.GND
  N1: IC1.P21, hc-sr1.Trig
  N2: IC1.P20, hc-sr1.Echo

notes:
  RED = VCC (5V)
  BLACK = GND
  GREEN = TRIG
  YELLOW = ECHO

custom parts:
  DIP - 28 pins: A DIP stand-in part for whatever IC you want. With 28 pins on a 300mil dual inline package (DIP) footprint.
