# Fritzing sketch LCD display 2x16 1602 (saved by Fritzing 0.9.9b)
breadboards: 1

parts:
  Part1 = LCD1602-I2C
  IC2 = DIP - 28 pins [chip_label=IC package="DIP (Dual Inline) [THT]"]

nets:
  GND: Part1.GND, IC2.GND
  VCC: Part1.VCC, IC2.VIN
  N1: Part1.SDA, IC2.P11
  N2: Part1.SCL, IC2.P12

custom parts:
  LCD1602-I2C: A standard character display, usually with 2x16 characters. Comes in many colors with LCM1602 IIC attached.
  DIP - 28 pins: A DIP stand-in part for whatever IC you want. With 28 pins on a 300mil dual inline package (DIP) footprint.
