# Fritzing sketch photoresistor (saved by Fritzing 0.9.6b)
breadboards: 1

parts:
  IC3 = DIP - 28 pins [chip_label=IC package="DIP (Dual Inline) [THT]"]
  R1 = PHOTOCELL [package=photocell-kit]
  Resistor = Resistor [tolerance=±5% resistance=10k package="0805 [SMD]"]

nets:
  N1: IC3.GND, Resistor.Pin_1
  N2: IC3.3V3, R1.P$2
  N3: IC3.P16, R1.P$1, Resistor.Pin_0

custom parts:
  DIP - 28 pins: A DIP stand-in part for whatever IC you want. With 28 pins on a 300mil dual inline package (DIP) footprint.
