# Fritzing sketch pycom_pysense (saved by Fritzing 0.9.3b)
breadboards: 1

parts:
  IC1 = DIP - 44 pins [chip_label="Pysense 2.0X" package="DIP (Dual Inline) [THT]"]
  IC2 = DIP - 28 pins [chip_label=Fipy package="DIP (Dual Inline) [THT]"]

nets:
  N1: IC1.P0, IC2.pin2
  N2: IC1.P1, IC2.pin3
  N3: IC1.P21, IC2.pin20
  N4: IC1.P22, IC2.pin19
  N5: IC1.GND, IC2.pin16
  N6: IC1.5V, IC2.pin15

notes:
  3.3V
  rail
  5V
  rail
  Pysense is used only as a programmer in this example. E.g. don't connect sensor pins/wires to it, all sensors should be connected on the breadboard and to the Fipy/Lopy4/Gpy

custom parts:
  DIP - 44 pins: A DIP stand-in part for whatever IC you want. With 44 pins on a 300mil dual inline package (DIP) footprint.
  DIP - 28 pins: A DIP stand-in part for whatever IC you want. With 28 pins on a 300mil dual inline package (DIP) footprint.
