# Fritzing sketch servo (saved by Fritzing 0.9.6b)
breadboards: 1

parts:
  IC1 = DIP - 28 pins [chip_label=IC package="DIP (Dual Inline) [THT]"]
  J1 = Basic Servo

nets:
  GND: IC1.GND, J1.gnd
  3V3: IC1.3V3, J1.vcc
  N1: IC1.P8, J1.pulse

custom parts:
  DIP - 28 pins: A DIP stand-in part for whatever IC you want. With 28 pins on a 300mil dual inline package (DIP) footprint.
