# Fritzing sketch halleffect (saved by Fritzing 0.9.6b)
breadboards: 1

parts:
  IC6 = DIP - 28 pins [chip_label=IC package="DIP (Dual Inline) [THT]"]
  U1 = A3144
  R1 = Resistor [tolerance=±5% resistance=10k package="0603 [SMD]"]

nets:
  N1: IC6.GND, U1.connector1
  N2: IC6.3V3, U1.connector2, R1.Pin_1
  N3: IC6.P16, U1.connector0, R1.Pin_0

notes:
  Your Sensor might differ from the one shown here. Ask a TA if you're unsure of how to connect

custom parts:
  DIP - 28 pins: A DIP stand-in part for whatever IC you want. With 28 pins on a 300mil dual inline package (DIP) footprint.
